// Logisim project circuito de soma.circ as structural Verilog: 5 circuits, main circuit main
module main (
  input  [3:0] in_1,
  output [3:0] out_2
);

  Comp_2 comp_2_1 (.in_1(in_1), .out_2(out_2));
endmodule

module ADD_1 (
  input  A,
  input  B,
  input  Vem_1,
  output S,
  output Vai_1
);

  wire and_1_out, and_2_out, or_1_out, xor_1_out;

  xor xor_1 (xor_1_out, B, A);
  or or_1 (or_1_out, Vem_1, B);
  and and_1 (and_1_out, B, Vem_1);
  xor xor_2 (S, Vem_1, xor_1_out);
  and and_2 (and_2_out, or_1_out, A);
  or or_2 (Vai_1, and_2_out, and_1_out);
endmodule

module ADD_4 (
  input  [3:0] B,
  input  [3:0] A,
  output Overflow,
  output [3:0] SOMA
);

  wire add_1_1_vai_1, add_1_3_vai_1, add_1_4_vai_1;

  // Probe on A
  ADD_1 add_1_1 (.A(A[2]), .B(B[2]), .Vem_1(add_1_3_vai_1), .S(SOMA[2]), .Vai_1(add_1_1_vai_1));
  ADD_1 add_1_2 (.A(A[3]), .B(B[3]), .Vem_1(add_1_1_vai_1), .S(SOMA[3]), .Vai_1(Overflow));
  ADD_1 add_1_3 (.A(A[1]), .B(B[1]), .Vem_1(add_1_4_vai_1), .S(SOMA[1]), .Vai_1(add_1_3_vai_1));
  // Probe on SOMA
  // Probe on B
  ADD_1 add_1_4 (.A(A[0]), .B(B[0]), .Vem_1(1'b0), .S(SOMA[0]), .Vai_1(add_1_4_vai_1));
endmodule

module Comp_2 (
  input  [3:0] in_1,
  output [3:0] out_2
);

  wire [3:0] not_3_out;

  // Probe on in_1
  not not_1 (not_3_out[1], in_1[1]);
  not not_2 (not_3_out[3], in_1[3]);
  not not_3 (not_3_out[0], in_1[0]);
  not not_4 (not_3_out[2], in_1[2]);
  ADD_4 add_4_1 (.A(not_3_out), .B(4'b0001), .SOMA(out_2));  // open: Overflow
  // Probe on out_2
endmodule

module Subtrator (
  input  [3:0] B,
  input  [3:0] A,
  output [3:0] out_3
);

  wire [3:0] comp_2_1_out_2;

  ADD_4 add_4_1 (.A(A), .B(comp_2_1_out_2), .SOMA(out_3));  // open: Overflow
  Comp_2 comp_2_1 (.in_1(B), .out_2(comp_2_1_out_2));
  // Probe on out_3
endmodule
